# Fritzing sketch m2m_eksamen (saved by Fritzing 0.9.3b)
breadboards: 1

parts:
  HiGrow_EPS32 = DOIT Esp32 DevKit v1 (30 pins long, 11 pins width) [part_number=ESP32S-PIN30]
  Q1 = Basic FET P-Channel [package="TO220 [THT]"]
  R1 = Resistor [tolerance=±5% resistance=1k package=THT]
  D1 = Rectifier Diode [part_number=1N4001 package="300 mil [THT]"]
  Water_Pump = DC Motor
  R2 = PHOTOCELL [package=photocell]
  R3 = Resistor [tolerance=±5% resistance=100k package=THT]

nets:
  N1: HiGrow_EPS32.D33, R2.P$1, R3.Pin_1
  N2: HiGrow_EPS32.D25, R1.Pin_0
  N3: HiGrow_EPS32.GND, Q1.source, D1.anode, R3.Pin_0
  N4: HiGrow_EPS32.VIN, Water_Pump.pin_1, R2.P$2
  N5: Q1.gate, R1.Pin_1
  N6: Q1.drain, D1.cathode, Water_Pump.pin_2

notes:
  DC vann pumpe
  HiGrow

custom parts:
  DOIT Esp32 DevKit v1 (30 pins long, 11 pins width): The DOIT Esp32 DevKit v1 is one of the development board created by DOIT to evaluate the ESP-WROOM-32 module. It is based on the ESP32 microcontroller that boasts Wifi, Bluetooth, Ethernet and Low Power support all in a single chip. (vanepp) made breadboard work, adjusted pin numbering and labels and reduced size of schematic and cleaned up pcb. This chip is 30pins long (2 x15) and 11 pins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
